# Fritzing sketch Jammer (saved by Fritzing 0.9.10b)
circuit board: 7.2cm x 4.5cm
breadboards: 1

parts:
  SSD1306 = Grove OLED 128x96
  NRF24L01 = NRF24L01+ Breakout Board [part_number=0]
  Button_2 = Pushbutton [package="[SMD]"]
  Button_1 = Pushbutton [package="[SMD]"]
  Ardunio_Nano = Arduino Nano (Rev3.0)

nets:
  GND: SSD1306.GND, NRF24L01.GND, Button_2.Pin_3, Button_2.Pin_4, Button_1.Pin_3, Button_1.Pin_4, Ardunio_Nano.GND
  VCC: SSD1306.VCC, Ardunio_Nano.3V3
  N1: SSD1306.SDA, Ardunio_Nano.A4
  N2: SSD1306.SCL, Ardunio_Nano.A5
  VCC_2: NRF24L01.VCC, Ardunio_Nano.5V
  N3: NRF24L01.CE, Ardunio_Nano.D9
  N4: NRF24L01.CS, Ardunio_Nano.D10
  N5: NRF24L01.SCK, Ardunio_Nano.D13/SCK
  N6: NRF24L01.MOSI, Ardunio_Nano.D11/MOSI
  N7: NRF24L01.MISO, Ardunio_Nano.D12/MISO
  N8: Button_2.Pin_1, Button_2.Pin_2, Ardunio_Nano.D2
  N9: Button_1.Pin_2, Ardunio_Nano.D7

// code stored in the sketch: Untitled.ino

